// Logisim project 1_bit_ALUT_AYHAM.circ as structural Verilog: 1 circuit, main circuit main
module main (
  input  B,
  input  A,
  input  CarryIn,
  input  B_invert,
  input  A_invenrt,
  input  [2:0] operation,
  output Result,
  output C_out
);

  wire adder_1_out, and_1_out, multiplexer_1_out, multiplexer_2_out, nor_1_out, not_1_out, not_2_out,
       or_1_out, xor_1_out;

  not not_1 (not_1_out, A);
  not not_2 (not_2_out, B);
  Multiplexer multiplexer_1 (.in0(not_2_out), .in1(B), .out(multiplexer_1_out), .sel(B_invert));  // open: en
  Multiplexer multiplexer_2 (.in0(not_1_out), .in1(A), .out(multiplexer_2_out), .sel(A_invenrt));  // open: en
  and and_1 (and_1_out, multiplexer_2_out, multiplexer_1_out);
  or or_1 (or_1_out, multiplexer_1_out, multiplexer_2_out);
  xor xor_1 (xor_1_out, multiplexer_1_out, multiplexer_2_out);
  nor nor_1 (nor_1_out, multiplexer_1_out, multiplexer_2_out);
  Adder #(.width(1)) adder_1 (
    .a(multiplexer_2_out), .b(multiplexer_1_out), .out(adder_1_out), .cin(CarryIn), .cout(C_out));
  Multiplexer #(.select(3)) multiplexer_3 (
    .in0(and_1_out), .in1(or_1_out), .in2(xor_1_out), .in3(nor_1_out), .in4(adder_1_out), .out(Result),
    .sel(operation));  // open: in5, in6, in7, en

  // Notes on the sheet:
  //   Ayham Al Ali - 201910486
endmodule
