// Logisim project 32bit_ALU_AYHAM.circ as structural Verilog: 2 circuits, main circuit ALU_1BIT
module ALU_1BIT (
  input  B_invert,
  input  CarryIn,
  input  [2:0] operation,
  input  A,
  input  B,
  input  Less,
  output Result,
  output C_out,
  output Set
);

  wire and_1_out, multiplexer_1_out, nor_1_out, not_1_out, or_1_out, xor_1_out;

  not not_1 (not_1_out, B);
  Multiplexer multiplexer_1 (.in0(not_1_out), .in1(B), .out(multiplexer_1_out), .sel(B_invert));  // open: en
  and and_1 (and_1_out, A, multiplexer_1_out);
  or or_1 (or_1_out, multiplexer_1_out, A);
  xor xor_1 (xor_1_out, multiplexer_1_out, A);
  nor nor_1 (nor_1_out, multiplexer_1_out, A);
  Adder #(.width(1)) adder_1 (.a(A), .b(multiplexer_1_out), .out(Set), .cin(CarryIn), .cout(C_out));
  Multiplexer #(.select(3)) multiplexer_2 (
    .in0(and_1_out), .in1(or_1_out), .in2(xor_1_out), .in3(nor_1_out), .in4(Set), .in5(Less), .out(Result),
    .sel(operation));  // open: in6, in7, en

  // Notes on the sheet:
  //   Ayham Al Ali - 201910486
endmodule

module Main (
  input  B_inv,
  input  [2:0] OP,
  input  [31:0] in_3,
  input  [31:0] in_4,
  output [31:0] OUTPUT,
  output ZeroFlag
);

  wire alu_1bit_1_c_out, alu_1bit_2_c_out, alu_1bit_3_c_out, alu_1bit_4_c_out, alu_1bit_5_c_out,
       alu_1bit_6_c_out, alu_1bit_7_c_out, alu_1bit_8_c_out, alu_1bit_9_c_out, alu_1bit_10_p6,
       alu_1bit_11_c_out, alu_1bit_12_c_out, alu_1bit_13_c_out, alu_1bit_14_c_out, alu_1bit_15_c_out,
       alu_1bit_16_c_out, alu_1bit_17_c_out, alu_1bit_18_c_out, alu_1bit_19_c_out, alu_1bit_20_c_out,
       alu_1bit_21_c_out, alu_1bit_22_c_out, alu_1bit_23_c_out, alu_1bit_24_c_out, alu_1bit_25_c_out,
       alu_1bit_26_c_out, alu_1bit_27_p6, alu_1bit_28_c_out, alu_1bit_29_c_out, alu_1bit_30_c_out,
       alu_1bit_31_c_out, alu_1bit_32_set;

  ALU_1BIT alu_1bit_1 (
    .Result(OUTPUT[0]), .B(in_4[0]), .A(in_3[0]), .CarryIn(B_inv), .B_invert(B_inv),
    .C_out(alu_1bit_1_c_out), .operation(OP), .Less(alu_1bit_32_set));  // open: Set
  ALU_1BIT alu_1bit_2 (
    .Result(OUTPUT[1]), .B(in_4[1]), .A(in_3[1]), .CarryIn(alu_1bit_1_c_out), .B_invert(B_inv),
    .C_out(alu_1bit_2_c_out), .operation(OP), .Less(1'b0));  // open: Set
  ALU_1BIT alu_1bit_3 (
    .Result(OUTPUT[2]), .B(in_4[2]), .A(in_3[2]), .CarryIn(alu_1bit_2_c_out), .B_invert(B_inv),
    .C_out(alu_1bit_3_c_out), .operation(OP), .Less(1'b0));  // open: Set
  ALU_1BIT alu_1bit_4 (
    .Result(OUTPUT[3]), .B(in_4[3]), .A(in_3[3]), .CarryIn(alu_1bit_3_c_out), .B_invert(B_inv),
    .C_out(alu_1bit_4_c_out), .operation(OP), .Less(1'b0));  // open: Set
  ALU_1BIT alu_1bit_5 (
    .Result(OUTPUT[4]), .B(in_4[4]), .A(in_3[4]), .CarryIn(alu_1bit_4_c_out), .B_invert(B_inv),
    .C_out(alu_1bit_5_c_out), .operation(OP), .Less(1'b0));  // open: Set
  ALU_1BIT alu_1bit_6 (
    .Result(OUTPUT[5]), .B(in_4[5]), .A(in_3[5]), .CarryIn(alu_1bit_5_c_out), .B_invert(B_inv),
    .C_out(alu_1bit_6_c_out), .operation(OP), .Less(1'b0));  // open: Set
  ALU_1BIT alu_1bit_7 (
    .Result(OUTPUT[6]), .B(in_4[6]), .A(in_3[6]), .CarryIn(alu_1bit_6_c_out), .B_invert(B_inv),
    .C_out(alu_1bit_7_c_out), .operation(OP), .Less(1'b0));  // open: Set
  ALU_1BIT alu_1bit_8 (
    .Result(OUTPUT[7]), .B(in_4[7]), .A(in_3[7]), .CarryIn(alu_1bit_7_c_out), .B_invert(B_inv),
    .C_out(alu_1bit_8_c_out), .operation(OP), .Less(1'b0));  // open: Set
  ALU_1BIT alu_1bit_9 (
    .Result(OUTPUT[8]), .B(in_4[8]), .A(in_3[8]), .CarryIn(alu_1bit_8_c_out), .B_invert(B_inv),
    .C_out(alu_1bit_9_c_out), .operation(OP), .Less(1'b0));  // open: Set
  // ALU_1BIT alu_1bit_10: pin names not known; wires that end beside it: in_3[9], in_4[9], 1'b0, B_inv, alu_1bit_9_c_out, alu_1bit_10_p6, OP, OUTPUT[9]
  ALU_1BIT alu_1bit_11 (
    .Result(OUTPUT[10]), .B(in_4[10]), .A(in_3[10]), .CarryIn(alu_1bit_10_p6), .B_invert(B_inv),
    .C_out(alu_1bit_11_c_out), .operation(OP), .Less(1'b0));  // open: Set
  ALU_1BIT alu_1bit_12 (
    .Result(OUTPUT[11]), .B(in_4[11]), .A(in_3[11]), .CarryIn(alu_1bit_11_c_out), .B_invert(B_inv),
    .C_out(alu_1bit_12_c_out), .operation(OP), .Less(1'b0));  // open: Set
  ALU_1BIT alu_1bit_13 (
    .Result(OUTPUT[12]), .B(in_4[12]), .A(in_3[12]), .CarryIn(alu_1bit_12_c_out), .B_invert(B_inv),
    .C_out(alu_1bit_13_c_out), .operation(OP), .Less(1'b0));  // open: Set
  ALU_1BIT alu_1bit_14 (
    .Result(OUTPUT[13]), .B(in_4[13]), .A(in_3[13]), .CarryIn(alu_1bit_13_c_out), .B_invert(B_inv),
    .C_out(alu_1bit_14_c_out), .operation(OP), .Less(1'b0));  // open: Set
  ALU_1BIT alu_1bit_15 (
    .Result(OUTPUT[14]), .B(in_4[14]), .A(in_3[14]), .CarryIn(alu_1bit_14_c_out), .B_invert(B_inv),
    .C_out(alu_1bit_15_c_out), .operation(OP), .Less(1'b0));  // open: Set
  ALU_1BIT alu_1bit_16 (
    .Result(OUTPUT[15]), .B(in_4[15]), .A(in_3[15]), .CarryIn(alu_1bit_15_c_out), .B_invert(B_inv),
    .C_out(alu_1bit_16_c_out), .operation(OP), .Less(1'b0));  // open: Set
  ALU_1BIT alu_1bit_17 (
    .Result(OUTPUT[16]), .B(in_4[16]), .A(in_3[16]), .CarryIn(alu_1bit_16_c_out), .B_invert(B_inv),
    .C_out(alu_1bit_17_c_out), .operation(OP), .Less(1'b0));  // open: Set
  ALU_1BIT alu_1bit_18 (
    .Result(OUTPUT[17]), .B(in_4[17]), .A(in_3[17]), .CarryIn(alu_1bit_17_c_out), .B_invert(B_inv),
    .C_out(alu_1bit_18_c_out), .operation(OP), .Less(1'b0));  // open: Set
  ALU_1BIT alu_1bit_19 (
    .Result(OUTPUT[18]), .B(in_4[18]), .A(in_3[18]), .CarryIn(alu_1bit_18_c_out), .B_invert(B_inv),
    .C_out(alu_1bit_19_c_out), .operation(OP), .Less(1'b0));  // open: Set
  ALU_1BIT alu_1bit_20 (
    .Result(OUTPUT[19]), .B(in_4[19]), .A(in_3[19]), .CarryIn(alu_1bit_19_c_out), .B_invert(B_inv),
    .C_out(alu_1bit_20_c_out), .operation(OP), .Less(1'b0));  // open: Set
  ALU_1BIT alu_1bit_21 (
    .Result(OUTPUT[20]), .B(in_4[20]), .A(in_3[20]), .CarryIn(alu_1bit_20_c_out), .B_invert(B_inv),
    .C_out(alu_1bit_21_c_out), .operation(OP), .Less(1'b0));  // open: Set
  ALU_1BIT alu_1bit_22 (
    .Result(OUTPUT[21]), .B(in_4[21]), .A(in_3[21]), .CarryIn(alu_1bit_21_c_out), .B_invert(B_inv),
    .C_out(alu_1bit_22_c_out), .operation(OP), .Less(1'b0));  // open: Set
  ALU_1BIT alu_1bit_23 (
    .Result(OUTPUT[22]), .B(in_4[22]), .A(in_3[22]), .CarryIn(alu_1bit_22_c_out), .B_invert(B_inv),
    .C_out(alu_1bit_23_c_out), .operation(OP), .Less(1'b0));  // open: Set
  ALU_1BIT alu_1bit_24 (
    .Result(OUTPUT[23]), .B(in_4[23]), .A(in_3[23]), .CarryIn(alu_1bit_23_c_out), .B_invert(B_inv),
    .C_out(alu_1bit_24_c_out), .operation(OP), .Less(1'b0));  // open: Set
  ALU_1BIT alu_1bit_25 (
    .Result(OUTPUT[24]), .B(in_4[24]), .A(in_3[24]), .CarryIn(alu_1bit_24_c_out), .B_invert(B_inv),
    .C_out(alu_1bit_25_c_out), .operation(OP), .Less(1'b0));  // open: Set
  ALU_1BIT alu_1bit_26 (
    .Result(OUTPUT[25]), .B(in_4[25]), .A(in_3[25]), .CarryIn(alu_1bit_25_c_out), .B_invert(B_inv),
    .C_out(alu_1bit_26_c_out), .operation(OP), .Less(1'b0));  // open: Set
  // ALU_1BIT alu_1bit_27: pin names not known; wires that end beside it: in_3[26], in_4[26], 1'b0, B_inv, alu_1bit_26_c_out, alu_1bit_27_p6, OP, OUTPUT[26]
  ALU_1BIT alu_1bit_28 (
    .Result(OUTPUT[27]), .B(in_4[27]), .A(in_3[27]), .CarryIn(alu_1bit_27_p6), .B_invert(B_inv),
    .C_out(alu_1bit_28_c_out), .operation(OP), .Less(1'b0));  // open: Set
  ALU_1BIT alu_1bit_29 (
    .Result(OUTPUT[28]), .B(in_4[28]), .A(in_3[28]), .CarryIn(alu_1bit_28_c_out), .B_invert(B_inv),
    .C_out(alu_1bit_29_c_out), .operation(OP), .Less(1'b0));  // open: Set
  ALU_1BIT alu_1bit_30 (
    .Result(OUTPUT[29]), .B(in_4[29]), .A(in_3[29]), .CarryIn(alu_1bit_29_c_out), .B_invert(B_inv),
    .C_out(alu_1bit_30_c_out), .operation(OP), .Less(1'b0));  // open: Set
  ALU_1BIT alu_1bit_31 (
    .Result(OUTPUT[30]), .B(in_4[30]), .A(in_3[30]), .CarryIn(alu_1bit_30_c_out), .B_invert(B_inv),
    .C_out(alu_1bit_31_c_out), .operation(OP), .Less(1'b0));  // open: Set
  ALU_1BIT alu_1bit_32 (
    .Result(OUTPUT[31]), .B(in_4[31]), .A(in_3[31]), .CarryIn(alu_1bit_31_c_out), .B_invert(B_inv),
    .operation(OP), .Set(alu_1bit_32_set), .Less(1'b0));  // open: C_out
  ExactlyOne xor_1 (
    .out(ZeroFlag), .in0(OUTPUT[0]), .in1(OUTPUT[1]), .in2(OUTPUT[2]), .in3(OUTPUT[3]), .in4(OUTPUT[4]),
    .in5(OUTPUT[5]), .in6(OUTPUT[6]), .in7(OUTPUT[7]), .in8(OUTPUT[8]), .in9(OUTPUT[9]), .in10(OUTPUT[10]),
    .in11(OUTPUT[11]), .in12(OUTPUT[12]), .in13(OUTPUT[13]), .in14(OUTPUT[14]), .in15(OUTPUT[15]),
    .in16(OUTPUT[16]), .in17(OUTPUT[17]), .in18(OUTPUT[18]), .in19(OUTPUT[19]), .in20(OUTPUT[20]),
    .in21(OUTPUT[21]), .in22(OUTPUT[22]), .in23(OUTPUT[23]), .in24(OUTPUT[24]), .in25(OUTPUT[25]),
    .in26(OUTPUT[26]), .in27(OUTPUT[27]), .in28(OUTPUT[28]), .in29(OUTPUT[29]), .in30(OUTPUT[30]),
    .in31(OUTPUT[31]));

  // Notes on the sheet:
  //   B
  //   A
  //   AYHAM AL ALI - 201910486
endmodule
